// Logisim project oisc.circ as structural Verilog: 1 circuit, main circuit main
module main (
  input  [7:0] DEBUG_IN
);

  wire and_1_out, CLK, demultiplexer_2_out0, demultiplexer_2_out1, not_1_out, not_2_out, OE_ADDR, OE_ALU,
       OE_DBGIN, OE_DBGOUT, OE_IO, OE_MEM, OE_PC, OE_RAM, OE_ROM, SUFFIX_SELECT, WE_DBGOUT, WE_HADDR, WE_IO,
       WE_LADDR, WE_MEM, WE_PC, WE_RAM, WE_X, WE_Y, Z_DETECT;
  wire [2:0] ADDRESS, SUFFIX_BITS;
  wire [3:0] MICRO_ADDR;
  wire [7:0] controlled_buffer_6_out, DATA, HADDR_q, HPC_q, LADDR_q, LPC_q, NOR_out, register_1_q, X_q, Y_q;
  wire [15:0] ADDR_DIRECT, rom_2_data;

  Register #(.trigger("high")) X (.D(DATA), .en(1'b1), .Q(X_q), .clk(WE_X));  // open: clr
  Register #(.trigger("high")) Y (.D(DATA), .en(1'b1), .Q(Y_q), .clk(WE_Y));  // open: clr
  assign ADDR_DIRECT[15:8] = OE_PC ? HPC_q : 8'bz;  // Controlled_Buffer controlled_buffer_1
  Register #(.trigger("high")) HPC (.D(ADDR_DIRECT[15:8]), .Q(HPC_q), .clk(WE_PC));  // open: en, clr
  Register #(.trigger("high")) HADDR (.D(DATA), .Q(HADDR_q), .clk(WE_HADDR));  // open: en, clr
  assign ADDR_DIRECT[15:8] = OE_ADDR ? HADDR_q : 8'bz;  // Controlled_Buffer controlled_buffer_2
  assign NOR_out = ~(X_q | Y_q);  // NOR_Gate NOR, 8 bits wide
  assign DATA = OE_ALU ? NOR_out : 8'bz;  // Controlled_Buffer controlled_buffer_3
  Register #(.trigger("high")) LPC (.D(ADDR_DIRECT[7:0]), .Q(LPC_q), .clk(WE_PC));  // open: en, clr
  assign ADDR_DIRECT[7:0] = OE_PC ? LPC_q : 8'bz;  // Controlled_Buffer controlled_buffer_4
  Register #(.trigger("high")) LADDR (.D(DATA), .Q(LADDR_q), .clk(WE_LADDR));  // open: en, clr
  assign ADDR_DIRECT[7:0] = OE_ADDR ? LADDR_q : 8'bz;  // Controlled_Buffer controlled_buffer_5
  Multiplexer #(.width(3), .enable("false")) multiplexer_1 (
    .in0(ADDR_DIRECT[2:0]), .in1(SUFFIX_BITS), .out(ADDRESS), .sel(SUFFIX_SELECT));
  not not_1 (not_1_out, WE_RAM);
  assign controlled_buffer_6_out = WE_RAM ? DATA : 8'bz;  // Controlled_Buffer controlled_buffer_6
  RAM #(.addrWidth(14), .bus("asynch")) ram_1 (
    .addr({ADDR_DIRECT[13:3], ADDRESS}), .data(controlled_buffer_6_out), .ld(not_1_out));  // open: sel, clr
  assign DATA = OE_RAM ? controlled_buffer_6_out : 8'bz;  // Controlled_Buffer controlled_buffer_7
  nor Z (Z_DETECT, NOR_out[0], NOR_out[1], NOR_out[2], NOR_out[3], NOR_out[4], NOR_out[5], NOR_out[6], NOR_out[7]);
  Clock CLK1 (.out(CLK));
  // Probe on DATA
  // Probe on {ADDR_DIRECT[15:3], ADDRESS}
  Pull_Resistor pull_resistor_1 (.node({ADDR_DIRECT[15:3], ADDRESS}));
  Counter #(.width(4), .max('hf)) counter_1 (
    .Q(MICRO_ADDR), .clk(not_2_out), .clr(and_1_out));  // open: load, D, count, carry
  not not_2 (not_2_out, CLK);
  ROM #(.addrWidth(15)) rom_1 (.addr({ADDR_DIRECT[14:3], ADDRESS}), .data(DATA), .sel(OE_ROM));
  and and_1 (and_1_out, MICRO_ADDR[1], MICRO_ADDR[3]);
  ROM #(.addrWidth(5), .dataWidth(16)) rom_2 (
    .addr({Z_DETECT, MICRO_ADDR}),
    .data({rom_2_data[15:12], SUFFIX_SELECT, SUFFIX_BITS, rom_2_data[7], WE_PC, WE_MEM, WE_HADDR, WE_LADDR, WE_X, WE_Y, rom_2_data[0]}),
    .sel(CLK));
  Demultiplexer #(.select(2), .enable("false")) demultiplexer_1 (
    .out2(WE_RAM), .out3(WE_IO), .in(WE_MEM), .sel(ADDR_DIRECT[15:14]));  // open: out0, out1
  Demultiplexer #(.select(2), .enable("false")) demultiplexer_2 (
    .out0(demultiplexer_2_out0), .out1(demultiplexer_2_out1), .out2(OE_RAM), .out3(OE_IO), .in(OE_MEM),
    .sel(ADDR_DIRECT[15:14]));
  Pull_Resistor pull_resistor_2 (.node({rom_2_data[15:12], SUFFIX_SELECT, SUFFIX_BITS, rom_2_data[7], WE_PC, WE_MEM, WE_HADDR, WE_LADDR, WE_X, WE_Y, rom_2_data[0]}));
  or or_1 (OE_ROM, demultiplexer_2_out0, demultiplexer_2_out1);
  buf buffer_1 (OE_ALU, rom_2_data[12]);
  buf buffer_2 (OE_MEM, rom_2_data[13]);
  buf buffer_3 (OE_PC, rom_2_data[14]);
  buf buffer_4 (OE_ADDR, rom_2_data[15]);
  LED led_1 (.in(DEBUG_IN[4]));
  LED led_2 (.in(DEBUG_IN[5]));
  LED led_3 (.in(DEBUG_IN[7]));
  LED led_4 (.in(DEBUG_IN[6]));
  Register #(.trigger("high")) register_1 (.D(DATA), .Q(register_1_q), .clk(WE_DBGOUT));  // open: en, clr
  LED led_5 (.in(register_1_q[5]));
  LED led_6 (.in(register_1_q[6]));
  LED led_7 (.in(register_1_q[4]));
  LED led_8 (.in(register_1_q[7]));
  Demultiplexer #(.enable("false")) demultiplexer_3 (.out0(OE_DBGOUT), .out1(OE_DBGIN), .in(OE_IO), .sel(ADDRESS[0]));
  Demultiplexer #(.enable("false")) demultiplexer_4 (.out0(WE_DBGOUT), .in(WE_IO), .sel(ADDRESS[0]));  // open: out1
  assign DATA = OE_DBGIN ? DEBUG_IN : 8'bz;  // Controlled_Buffer controlled_buffer_8
  LED led_9 (.in(DEBUG_IN[2]));
  LED led_10 (.in(DEBUG_IN[0]));
  LED led_11 (.in(DEBUG_IN[1]));
  LED led_12 (.in(DEBUG_IN[3]));
  assign DATA = OE_DBGOUT ? {8{1'b0}} : 8'bz;  // Controlled_Buffer controlled_buffer_9
  LED led_13 (.in(register_1_q[3]));
  LED led_14 (.in(register_1_q[0]));
  LED led_15 (.in(register_1_q[1]));
  LED led_16 (.in(register_1_q[2]));

  // Other names for the same wires on the sheet: ADDRESS[15:3] = ADDR_DIRECT[15:3]

  // Notes on the sheet:
  //   RAM
  //   ALU
  //   REGISTERS
  //   buffered for data holdoff (caps irl)
  //   PROGRAM ROM
  //   MAPPED MEMORY
  //   contents of rom_1 (hex, n*v repeats v):
  //   bf d0 1 d8 0 8 0 8 bf d0 1 d9 0 10 0 10 bf d0 bf d0 0 18 0 18 bf d1 1 d8 0 20 0 20 bf d1 1 da 0 28 0
  //   28 bf d1 bf d1 0 30 0 30 bf d2 1 d8 0 38 0 38 bf d2 1 db 0 40 0 40 bf d2 bf d2 0 48 0 48 bf d3 1 d8
  //   0 50 0 50 bf d3 1 dc 0 58 0 58 bf d3 bf d3 0 60 0 60 bf d4 1 d8 0 68 0 68 bf d4 1 d9 0 70 0 70 bf d4
  //   bf d4 0 78 0 78 bf d5 1 d8 0 80 0 80 bf d5 1 dd 0 88 0 88 bf d5 bf d5 0 90 0 90 bf d6 1 d8 0 98 0 98
  //   bf d6 1 d9 0 a0 0 a0 bf d6 bf d6 0 a8 0 a8 bf d7 1 d8 0 b0 0 b0 bf d7 1 dd 0 b8 0 b8 bf d7 bf d7 0
  //   c0 0 c0 bf d8 1 d8 0 c8 0 c8 bf d8 1 d9 0 d0 0 d0 bf d8 bf d8 0 d8 0 d8 bf d9 1 d8 0 e0 0 e0 bf d9 1
  //   da 0 e8 0 e8 bf d9 bf d9 0 f0 0 f0 bf dc 1 d8 0 f8 0 f8 bf dc 1 d9 1 0 1 0 bf dc bf dc 1 8 1 8 bf dd
  //   1 d8 1 10 1 10 bf dd 1 de 1 18 1 18 bf dd bf dd 1 20 1 20 bf de 1 d8 1 28 1 28 bf de 1 d9 1 30 1 30
  //   bf de bf de 1 38 1 38 bf df 1 d8 1 40 1 40 bf df 1 de 1 48 1 48 bf df bf df 1 50 1 50 bf e0 1 d8 1
  //   58 1 58 bf e0 1 d9 1 60 1 60 bf e0 bf e0 1 68 1 68 bf e1 1 d8 1 70 1 70 bf e1 1 df 1 78 1 78 bf e1
  //   bf e1 1 80 1 80 bf e2 1 d8 1 88 1 88 bf e2 1 db 1 90 1 90 bf e2 bf e2 1 98 1 98 bf e3 1 d8 1 a0 1 a0
  //   bf e3 1 dc 1 a8 1 a8 bf e3 bf e3 1 b0 1 b0 bf ff bf ff 1 b0 1 b0 328*0 ff 7*0 ff bf f0 3 0 d8 e0 f1
  //   MICROCODE
  //   contents of rom_2 (hex, n*v repeats v):
  //   6a10 6b08 a002 6810 6908 a004 9020 6c10 6d08 8040 1 5*0 6a10 6b08 a002 6810 6908 a004 9020 6e10 6f08
  //   8040 1
  //   I/O
endmodule
